# Fritzing sketch schema (saved by Fritzing 0.7.11b)
breadboards: 1

parts:
  T1 = LM35 Temperature Sensor [package="TO92 [THT]"]
  Afficheur = IC, SIP package, 5 pins [chip_label=Afficheur]
  Arduino1 = Arduino

nets:
  5V: T1.+Vs, Afficheur.pin1, Arduino1.+5V
  N1: T1.Vout, Arduino1.A0
  GND: T1.GND, Afficheur.pin2, Arduino1.GND
  N2: Afficheur.pin3, Arduino1.D11
  N3: Afficheur.pin4, Arduino1.D13
  N4: Afficheur.pin5, Arduino1.D10
